# Fritzing sketch pumpa (saved by Fritzing 0.9.3b)

parts:
  part = Raspberry Pi Pico W
  WATER_PUMP1 = water pump/motor
  KY-1 = Keyes Relay [package=THT]

nets:
  N1: part.pin_8, part.pin_18, part.pin_42, WATER_PUMP1.pin_1, KY-1.ground
  N2: part.pin_32, KY-1.signal
  N3: part.pin_36, KY-1.power
  N4: WATER_PUMP1.pin_2, KY-1.NC, KY-1.C, KY-1.NO

custom parts:
  Raspberry Pi Pico W: Raspberry Pi Pico W. Based around the RP2040 microcontroller the Pico W is a low cost microcontroller device bringing Raspberry Pi quality, cost, and easy of use to the microcontroller space. The areas marked KEEPOUT in pcb silkscreen should not have traces running through them to avoid shorts on a soldered in module!
  water pump/motor: WATER PUMP BY ARDUBLOCKTR
  Keyes Relay: The Keyes 5V relay module is suitable for SCM development, home appliance control. It uses a 5V~12V TIL control signal which can control DC / AC signal.
