# Fritzing sketch senzor (saved by Fritzing 0.9.3b)
breadboards: 1

parts:
  Mod1 = Raspberry Pi Pico W
  Part1 = Soil Moisture Sensor

nets:
  N1: Mod1.pin_13, Mod1.pin_38, Part1.GND
  N2: Mod1.pin_31, Part1.SIG
  N3: Mod1.pin_36, Part1.VCC

custom parts:
  Raspberry Pi Pico W: Raspberry Pi Pico W. Based around the RP2040 microcontroller the Pico W is a low cost microcontroller device bringing Raspberry Pi quality, cost, and easy of use to the microcontroller space. The areas marked KEEPOUT in pcb silkscreen should not have traces running through them to avoid shorts on a soldered in module!
